# Fritzing sketch LC-test-circuit (saved by Fritzing 0.9.2b)

parts:
  Part1 = Arduino Uno (Rev3)
  C1 = Ceramic Capacitor [capacitance=10µF package="100 mil [THT, multilayer]"]
  R1 = Resistor [tolerance=±5% resistance=10k package=THT]
  R2 = Resistor [tolerance=±5% resistance=10k package=THT]
  L1 = Inductor [package="0805 [SMD]"]

nets:
  N1: Part1.A0, C1.0, L1.pin_1
  N2: Part1.5V, R1.Pin_0
  N3: Part1.GND, R2.Pin_0
  N4: C1.1, R1.Pin_1, R2.Pin_1, L1.pin_0
