# Fritzing sketch LR-test-circuit (saved by Fritzing 0.9.2b)

parts:
  Part1 = Arduino Uno (Rev3)
  L1 = Inductor [package="0805 [SMD]"]
  R2 = Resistor [tolerance=±5% resistance=2.2 package=THT]

nets:
  N1: Part1.A4/SDA, L1.pin_0
  N2: Part1.GND, R2.Pin_0
